// Logisim project lab2.circ as structural Verilog: 2 circuits, main circuit main
module main (
  input  In1A,
  input  In1B,
  input  In1C,
  output Out1
);

  wire and_1_out, and_2_out, and_3_out;

  and and_1 (and_1_out, ~In1A, In1B, ~In1C);  // AND_Gate
  and and_2 (and_2_out, In1A, ~In1B, ~In1C);  // AND_Gate
  and and_3 (and_3_out, In1A, In1B, In1C);
  or or_1 (Out1, and_1_out, and_2_out, and_3_out);
endmodule

module Equation_2 (
  input  In2A,
  input  In2B,
  input  In2C,
  input  In2D,
  output Out2
);

  wire and_1_out, and_2_out, and_3_out, and_4_out;

  and and_1 (and_1_out, ~In2A, ~In2B, In2C, ~In2D);  // AND_Gate
  and and_2 (and_2_out, ~In2A, In2B, In2C, In2D);  // AND_Gate
  and and_3 (and_3_out, In2A, ~In2B, In2C, ~In2D);  // AND_Gate
  and and_4 (and_4_out, In2A, In2B, In2C, ~In2D);  // AND_Gate
  or or_1 (Out2, and_1_out, and_2_out, and_3_out, and_4_out);

  // Notes on the sheet:
  //   (A'B'CD')+(A'BCD)+(AB'CD')+(ABCD')
endmodule
