// Logisim project lab5.circ as structural Verilog: 7 circuits, main circuit main
module main (
  input  Reset,
  input  [2:0] in_2,
  output [3:0] Probe1
);

  wire clk_out;

  Clock #(.highDuration(4), .lowDuration(4)) clk (.out(clk_out));
  Clock sysclk ();  // open: out
  Universal universal_1 (.clk(clk_out), .Reset(Reset), .Sel(in_2), .UniOut(Probe1));
  Hex_Digit_Display hex_digit_display_1 (.value(Probe1));  // open: dp
endmodule

module AsUpCounter (
  input  clk,
  input  rst,
  output [3:0] out_3
);

  wire d_ff_1_qn, d_ff_2_qn, d_ff_3_qn, d_ff_4_qn;

  D_Flip_Flop d_ff_1 (.D(d_ff_1_qn), .clk(clk), .Q(out_3[0]), .Qn(d_ff_1_qn), .reset(rst));  // open: preset
  D_Flip_Flop d_ff_2 (.D(d_ff_2_qn), .clk(d_ff_1_qn), .Q(out_3[1]), .Qn(d_ff_2_qn), .reset(rst));  // open: preset
  D_Flip_Flop d_ff_3 (.D(d_ff_3_qn), .clk(d_ff_2_qn), .Q(out_3[2]), .Qn(d_ff_3_qn), .reset(rst));  // open: preset
  D_Flip_Flop d_ff_4 (.D(d_ff_4_qn), .clk(d_ff_3_qn), .Q(out_3[3]), .Qn(d_ff_4_qn), .reset(rst));  // open: preset

  // Notes on the sheet:
  //   Asynchronous Up Counter
endmodule

module AsDownCounter (
  input  clk,
  input  Reset,
  output [3:0] Down
);

  wire d_ff_1_qn, d_ff_2_qn, d_ff_3_qn, d_ff_4_qn;

  D_Flip_Flop d_ff_1 (.D(d_ff_1_qn), .clk(clk), .Q(Down[0]), .Qn(d_ff_1_qn), .preset(Reset));  // open: reset
  D_Flip_Flop d_ff_2 (.D(d_ff_2_qn), .clk(Down[0]), .Q(Down[1]), .Qn(d_ff_2_qn), .preset(Reset));  // open: reset
  D_Flip_Flop d_ff_3 (.D(d_ff_3_qn), .clk(Down[1]), .Q(Down[2]), .Qn(d_ff_3_qn), .preset(Reset));  // open: reset
  D_Flip_Flop d_ff_4 (.D(d_ff_4_qn), .clk(Down[2]), .Q(Down[3]), .Qn(d_ff_4_qn), .preset(Reset));  // open: reset

  // Notes on the sheet:
  //   Asyncgronous Down Counter
endmodule

module AsDecadeCounter (
  input  clk,
  input  Reset,
  output [3:0] Decade
);

  wire and_1_out, d_ff_1_qn, d_ff_2_qn, d_ff_3_qn, d_ff_4_qn, or_1_out;

  D_Flip_Flop d_ff_1 (.D(d_ff_1_qn), .clk(clk), .Q(Decade[0]), .Qn(d_ff_1_qn), .reset(or_1_out));  // open: preset
  or or_1 (or_1_out, Reset, and_1_out);
  D_Flip_Flop d_ff_2 (.D(d_ff_2_qn), .clk(d_ff_1_qn), .Q(Decade[1]), .Qn(d_ff_2_qn), .reset(or_1_out));  // open: preset
  D_Flip_Flop d_ff_3 (.D(d_ff_3_qn), .clk(d_ff_2_qn), .Q(Decade[2]), .Qn(d_ff_3_qn), .reset(or_1_out));  // open: preset
  D_Flip_Flop d_ff_4 (.D(d_ff_4_qn), .clk(d_ff_3_qn), .Q(Decade[3]), .Qn(d_ff_4_qn), .reset(or_1_out));  // open: preset
  and and_1 (and_1_out, Decade[3], Decade[1]);
endmodule

module SynRingCounter (
  input  clk,
  input  Reset,
  output [3:0] Ring
);

  D_Flip_Flop d_ff_1 (.D(Ring[3]), .clk(clk), .Q(Ring[0]), .preset(Reset));  // open: Qn, reset
  D_Flip_Flop d_ff_2 (.D(Ring[0]), .clk(clk), .Q(Ring[1]), .reset(Reset));  // open: Qn, preset
  D_Flip_Flop d_ff_3 (.D(Ring[1]), .clk(clk), .Q(Ring[2]), .reset(Reset));  // open: Qn, preset
  D_Flip_Flop d_ff_4 (.D(Ring[2]), .clk(clk), .Q(Ring[3]), .reset(Reset));  // open: Qn, preset

  // Notes on the sheet:
  //   Synchronous Ring Counter
endmodule

module JohnsonCounter (
  input  clk,
  input  Reset,
  output [3:0] Johnson
);

  wire d_ff_4_qn;

  D_Flip_Flop d_ff_1 (.D(d_ff_4_qn), .clk(clk), .Q(Johnson[0]), .preset(Reset));  // open: Qn, reset
  D_Flip_Flop d_ff_2 (.D(Johnson[0]), .clk(clk), .Q(Johnson[1]), .reset(Reset));  // open: Qn, preset
  D_Flip_Flop d_ff_3 (.D(Johnson[1]), .clk(clk), .Q(Johnson[2]), .reset(Reset));  // open: Qn, preset
  D_Flip_Flop d_ff_4 (.D(Johnson[2]), .clk(clk), .Q(Johnson[3]), .Qn(d_ff_4_qn), .reset(Reset));  // open: preset
endmodule

module Universal (
  input  clk,
  input  Reset,
  input  [2:0] Sel,
  output [3:0] UniOut
);

  wire [3:0] asdecadecounter_1_decade, asdowncounter_1_down, asupcounter_1_out_3, johnsoncounter_1_johnson,
       synringcounter_1_ring;

  AsUpCounter asupcounter_1 (.clk(clk), .rst(Reset), .out_3(asupcounter_1_out_3));
  AsDownCounter asdowncounter_1 (.clk(clk), .Reset(Reset), .Down(asdowncounter_1_down));
  AsDecadeCounter asdecadecounter_1 (.clk(clk), .Reset(Reset), .Decade(asdecadecounter_1_decade));
  SynRingCounter synringcounter_1 (.clk(clk), .Reset(Reset), .Ring(synringcounter_1_ring));
  JohnsonCounter johnsoncounter_1 (.clk(clk), .Reset(Reset), .Johnson(johnsoncounter_1_johnson));
  Multiplexer #(.select(3), .width(4)) multiplexer_1 (
    .in0(asupcounter_1_out_3), .in1(asdowncounter_1_down), .in2(asdecadecounter_1_decade),
    .in3(synringcounter_1_ring), .in4(johnsoncounter_1_johnson), .out(UniOut), .sel(Sel));  // open: in5, in6, in7

  // Notes on the sheet:
  //   Universal counter
endmodule
